# Fritzing sketch IR (saved by Fritzing 0.9.3b)
breadboards: 1

parts:
  Part1 = Arduino Uno (Rev3)
  LED1 = LED - 5mm [color="Infrared (850nm)" package="5 mm [THT]"]
  R1 = Resistor [tolerance=±5% resistance=470 package=THT]
  R2 = Resistor [tolerance=±5% resistance=470 package=THT]
  R3 = Resistor [tolerance=±5% resistance=10k package=THT]
  LED2 = LED - 5mm [color="Infrared (940nm)" package="5 mm [THT]"]

nets:
  N1: Part1.D2, R2.Pin_1, R3.Pin_0
  N2: Part1.D7, R1.Pin_1
  N3: Part1.5V, LED2.cathode
  N4: Part1.GND, LED1.cathode, R3.Pin_1
  N5: LED1.anode, R1.Pin_0
  N6: R2.Pin_0, LED2.anode
